# Fritzing sketch dht22-schema (saved by Fritzing 0.9.4)
breadboards: 1

parts:
  Part1 = Arduino Uno (Rev3)
  RHT1 = Humidity and Temperature Sensor RHT03
  R2 = Resistor [tolerance=±1% resistance=4.7k package=THT]
  C1 = Electrolytic Capacitor [capacitance=100nF package="0605 [SMD, electrolytic]"]

nets:
  N1: Part1.D2, RHT1.Data-signal, R2.Pin_0
  5V: Part1.5V, RHT1.Vcc, R2.Pin_1, C1.+
  N2: Part1.GND, RHT1.GND_2, C1.-
